// Logisim project CPU.circ as structural Verilog: 4 circuits, main circuit main
module main (
  output [7:0] address,
  output [7:0] r0,
  output [1:0] addrsel,
  output [7:0] r1,
  output [7:0] r2,
  output [7:0] r3,
  output [7:0] datain,
  output [1:0] aluop,
  output [7:0] dval,
  output [7:0] dbus,
  output [7:0] aluout,
  output [7:0] sbus,
  output [7:0] out_13,
  output pcsel,
  output [1:0] phase,
  output pcload
);

  wire clock_1_out, clock_2_out, clock_3_out, clock_4_out, dwrite, imload, irload, readwrite,
       register_file_731404a5_1_negative, register_file_731404a5_1_zero;
  wire [1:0] dregsel, regsel, sregsel;
  wire [7:0] multiplexer_2_out, pc_adder_e7edaaa0_1_pc_out_eb01c7b6, register_1_q, register_2_q, register_3_q;

  Clock clock_1 (.out(clock_1_out));
  RAM #(.enables("line"), .trigger("falling")) ram_1 (
    .addr(address), .we(readwrite), .clk(clock_1_out), .din(dbus));  // open: dout
  Multiplexer #(.enable("true"), .select(2), .width(8)) multiplexer_1 (
    .in0(register_3_q), .in1(register_2_q), .in2(sbus), .in3(dbus), .out(address), .sel(addrsel));  // open: en
  Register register_1 (.D(datain), .en(irload), .clk(clock_2_out), .Q(register_1_q));  // open: clr
  Clock clock_2 (.out(clock_2_out));
  Register register_2 (.D(datain), .en(imload), .clk(clock_3_out), .Q(register_2_q));  // open: clr
  Clock clock_3 (.out(clock_3_out));
  Decode_Logic_78b07538 decode_logic_78b07538_1 (
    .irvalue(register_1_q), .zero(register_file_731404a5_1_zero),
    .negative(register_file_731404a5_1_negative), .addrsel(addrsel), .irload(irload), .regsel(regsel),
    .dregsel(dregsel), .sregsel(sregsel), .aluop(aluop), .pcload(pcload), .imload(imload), .dwrite(dwrite),
    .pcsel(pcsel), .phase(phase), .readwrite(readwrite));
  Multiplexer #(.enable("true"), .width(8)) multiplexer_2 (
    .in0(register_2_q), .in1(pc_adder_e7edaaa0_1_pc_out_eb01c7b6), .out(multiplexer_2_out), .sel(pcsel));  // open: en
  Multiplexer #(.enable("true"), .select(2), .width(8)) multiplexer_3 (
    .in0(register_2_q), .in1(sbus), .in2(datain), .in3(aluout), .out(dval), .sel(regsel));  // open: en
  Clock clock_4 (.out(clock_4_out));
  PC_Adder_e7edaaa0 pc_adder_e7edaaa0_1 (
    .PC_in_8df114b0(register_3_q), .PC_out_eb01c7b6(pc_adder_e7edaaa0_1_pc_out_eb01c7b6));
  Register_File_731404a5 register_file_731404a5_1 (
    .dval(dval), .dwrite(dwrite), .sregsel(sregsel), .dregsel(dregsel), .Zero(register_file_731404a5_1_zero),
    .Negative(register_file_731404a5_1_negative), .r3(r3), .r2(r2), .r0(r0), .r1(r1), .dbus(dbus), .sbus(sbus));
  Register register_3 (.D(multiplexer_2_out), .en(pcload), .clk(clock_4_out), .Q(register_3_q));  // open: clr
  // ALU alu_1: pin names not known; wires that end beside it: dbus, sbus, aluop, aluout

  assign out_13 = aluout;

  // Notes on the sheet:
  //   address bus
  //   RAM
  //   dataout bus
  //   datain   bus
  //   IR
  //   Immed
  //   Decode
  //   Logic
  //   8-bit Hardwired CPU
  //   +
  //   PC Adder
  //   Regs
  //   PC
  //   Register
  //   Values
  //   ALU
endmodule

module Register_File_731404a5 (
  input  dwrite,
  input  [1:0] dregsel,
  input  [7:0] dval,
  input  [1:0] sregsel,
  output [7:0] r0,
  output [7:0] dbus,
  output [7:0] r1,
  output Zero,
  output [7:0] r2,
  output [7:0] r3,
  output Negative,
  output [7:0] sbus
);

  wire clock_1_out, demultiplexer_1_out0, demultiplexer_1_out1, demultiplexer_1_out2, demultiplexer_1_out3,
       or_1_out;

  Demultiplexer #(.enable("true"), .select(2)) demultiplexer_1 (
    .out0(demultiplexer_1_out0), .out1(demultiplexer_1_out1), .out2(demultiplexer_1_out2),
    .out3(demultiplexer_1_out3), .in(dwrite), .sel(dregsel));  // open: en
  Register register_1 (.D(dval), .en(demultiplexer_1_out0), .clk(clock_1_out), .Q(r0));  // open: clr
  Register register_2 (.D(dval), .en(demultiplexer_1_out1), .clk(clock_1_out), .Q(r1));  // open: clr
  Register register_3 (.D(dval), .en(demultiplexer_1_out2), .clk(clock_1_out), .Q(r2));  // open: clr
  Register register_4 (.D(dval), .en(demultiplexer_1_out3), .clk(clock_1_out), .Q(r3));  // open: clr
  Clock clock_1 (.out(clock_1_out));
  Multiplexer #(.enable("true"), .select(2), .width(8)) multiplexer_1 (
    .in0(r0), .in1(r1), .in2(r2), .in3(r3), .out(dbus), .sel(dregsel));  // open: en
  Multiplexer #(.enable("true"), .select(2), .width(8)) multiplexer_2 (
    .in0(r0), .in1(r1), .in2(r2), .in3(r3), .out(sbus), .sel(sregsel));  // open: en
  not not_1 (Zero, or_1_out);
  or or_1 (or_1_out, dbus[0], dbus[1], dbus[2], dbus[3], dbus[4], dbus[5], dbus[6], dbus[7]);

  assign Negative = dbus[7];

  // Other names for the same wires on the sheet: drs[1:0] = dregsel

  // Notes on the sheet:
  //   Register File
endmodule

module PC_Adder_e7edaaa0 (
  input  [7:0] PC_in_8df114b0,
  output [7:0] PC_out_eb01c7b6
);

  Adder adder_1 (.a(PC_in_8df114b0), .b(8'h1), .out(PC_out_eb01c7b6), .cin(1'b0));  // open: cout

  // Notes on the sheet:
  //   PC Adder
endmodule

module Decode_Logic_78b07538 (
  input  [7:0] irvalue,
  input  zero,
  input  negative,
  output [1:0] phase,
  output [1:0] dregsel,
  output [1:0] sregsel,
  output [1:0] aluop,
  output irload,
  output imload,
  output pcsel,
  output readwrite,
  output pcload,
  output [1:0] regsel,
  output dwrite,
  output [1:0] addrsel
);

  wire and_1_out, and_2_out, and_3_out, and_4_out, and_5_out, clock_1_out, d_ff_2_qn, multiplexer_3_out,
       multiplexer_7_out, not_1_out, not_2_out, not_3_out, not_4_out, or_1_out;
  wire [1:0] multiplexer_1_out, multiplexer_11_out;

  not not_1 (not_1_out, zero);
  not not_2 (not_2_out, negative);
  and and_1 (and_1_out, not_1_out, not_2_out);
  Multiplexer #(.enable("true"), .select(4), .width(2)) multiplexer_1 (
    .in0(2'b11), .in1(2'b11), .in2(2'b11), .in3(2'b11), .in4(2'b10), .in5(2'b00), .in6(2'b01), .in7(2'b00),
    .in8(2'b00), .in9(2'b00), .in10(2'b00), .in11(2'b00), .in12(2'b10), .in13(2'b00), .in14(2'b00),
    .in15(2'b00), .out(multiplexer_1_out), .sel(irvalue[7:4]));  // open: en
  Multiplexer #(.enable("true"), .select(2)) multiplexer_2 (
    .in0(1'b1), .in1(1'b0), .in2(1'b0), .in3(1'b0), .out(irload), .sel(phase));  // open: en
  not not_3 (not_3_out, irvalue[6]);
  Multiplexer #(.enable("true"), .select(2)) multiplexer_3 (
    .in0(zero), .in1(not_1_out), .in2(and_1_out), .in3(negative), .out(multiplexer_3_out), .sel(irvalue[5:4]));  // open: en
  and and_2 (and_2_out, not_3_out, irvalue[7], multiplexer_3_out);
  and and_3 (and_3_out, irvalue[4], irvalue[5], irvalue[6], irvalue[7]);
  Multiplexer #(.enable("true"), .select(2), .width(2)) multiplexer_4 (
    .in0(2'b00), .in1(2'b00), .in2(multiplexer_1_out), .in3(2'b00), .out(regsel), .sel(phase));  // open: en
  or or_1 (or_1_out, and_2_out, and_3_out);
  Multiplexer #(.enable("true"), .select(2)) multiplexer_5 (
    .in0(1'b1), .in1(irvalue[7]), .in2(or_1_out), .in3(1'b0), .out(pcload), .sel(phase));  // open: en
  Multiplexer #(.enable("true"), .select(2)) multiplexer_6 (
    .in0(1'b0), .in1(irvalue[7]), .in2(1'b0), .in3(1'b0), .out(imload), .sel(phase));  // open: en
  Multiplexer #(.enable("true"), .select(4)) multiplexer_7 (
    .in0(1'b1), .in1(1'b1), .in2(1'b1), .in3(1'b1), .in4(1'b1), .in5(1'b0), .in6(1'b1), .in7(1'b0),
    .in8(1'b0), .in9(1'b0), .in10(1'b0), .in11(1'b0), .in12(1'b1), .in13(1'b0), .in14(1'b1), .in15(1'b0),
    .out(multiplexer_7_out), .sel(irvalue[7:4]));  // open: en
  Clock clock_1 (.out(clock_1_out));
  not not_4 (not_4_out, irvalue[5]);
  Multiplexer #(.enable("true"), .select(2)) multiplexer_8 (
    .in0(1'b0), .in1(1'b0), .in2(multiplexer_7_out), .in3(1'b0), .out(dwrite), .sel(phase));  // open: en
  D_Flip_Flop d_ff_1 (.clk(clock_1_out), .D(d_ff_2_qn), .Q(phase[0]), .reset(and_5_out));  // open: Qn, preset
  D_Flip_Flop d_ff_2 (
    .clk(clock_1_out), .D(phase[0]), .Q(phase[1]), .Qn(d_ff_2_qn), .preset(and_5_out));  // open: reset
  Multiplexer #(.enable("true"), .select(2)) multiplexer_9 (
    .in0(1'b1), .in1(1'b1), .in2(1'b0), .in3(1'b0), .out(pcsel), .sel(phase));  // open: en
  and and_4 (and_4_out, irvalue[4], not_4_out, irvalue[6]);
  and and_5 (and_5_out, phase[1], phase[0]);
  Multiplexer #(.enable("true"), .select(2)) multiplexer_10 (
    .in0(1'b0), .in1(1'b0), .in2(and_4_out), .in3(1'b0), .out(readwrite), .sel(phase));  // open: en
  Multiplexer #(.enable("true"), .select(4), .width(2)) multiplexer_11 (
    .in0(2'b00), .in1(2'b00), .in2(2'b00), .in3(2'b00), .in4(2'b10), .in5(2'b10), .in6(2'b00), .in7(2'b00),
    .in8(2'b00), .in9(2'b00), .in10(2'b00), .in11(2'b00), .in12(2'b00), .in13(2'b01), .in14(2'b01),
    .in15(2'b00), .out(multiplexer_11_out), .sel(irvalue[7:4]));  // open: en
  Multiplexer #(.enable("true"), .select(2), .width(2)) multiplexer_12 (
    .in0(2'b00), .in1(2'b00), .in2(multiplexer_11_out), .in3(2'b00), .out(addrsel), .sel(phase));  // open: en

  assign aluop = irvalue[5:4];
  assign dregsel = irvalue[3:2];
  assign sregsel = irvalue[1:0];

  // Other names for the same wires on the sheet: irbit4 = irvalue[4]; op1op2[3:0] = irvalue[7:4];
  //   op2[1:0] = irvalue[5:4]; irbit5 = irvalue[5]; irbit6 = irvalue[6]; op1[1:0] = irvalue[7:6]; irbit7 = irvalue[7];
  //   rd[1:0] = irvalue[3:2]; rs[1:0] = irvalue[1:0]

  // Notes on the sheet:
  //   IR Load
  //   PC Load
  //   Register Select
  //   Immed Load
  //   Decode Logic
  //   Dest Reg Write
  //   PC Select
  //   Read/Write
  //   Phase
  //   Counter
  //   Address Select
endmodule
