// Logisim project project.circ as structural Verilog: 6 circuits, main circuit nieuporzadkowane
module nieuporzadkowane (
);

  wire Clk, comparator_1_eq, d_ff_1_qn, decoder_1_out2, decoder_1_out3, decoder_1_out4, decoder_1_out5,
       decoder_1_out6, decoder_1_out7, decoder_1_out8, decoder_1_out9, decoder_1_out10, decoder_1_out11,
       decoder_1_out12, jie, jine, LVRAM1, not_1_out, nullChar, oo, or_1_out, or_2_out, or_3_out, print,
       pwr_out, rst;
  wire [3:0] rom_1_data_2;
  wire [7:0] adder_1_out, adder_2_out, controlled_buffer_1_out, counter_1_q, counter_2_q, divider_1_out,
       divider_1_rem, multiplier_1_out, ram_2_dout, ramData, reg1_q, reg2_q, rom_1_data, subtractor_1_out;

  Clock u_clk (.out(Clk));
  Button Reset (.out(rst));
  Button pwr (.out(pwr_out));
  D_Flip_Flop d_ff_1 (.D(d_ff_1_qn), .clk(pwr_out), .Q(oo), .Qn(d_ff_1_qn));  // open: preset, reset
  RAM #(.enables("line")) ram_1 (
    .addr(rom_1_data), .we(or_1_out), .clk(Clk), .din(controlled_buffer_1_out), .dout(ramData));
  or or_1 (or_1_out, decoder_1_out4, decoder_1_out5, decoder_1_out6, decoder_1_out7, decoder_1_out8, decoder_1_out12, decoder_1_out11);
  Register reg1 (.D(ramData), .en(decoder_1_out2), .clk(Clk), .Q(reg1_q), .clr(rst));
  Register reg2 (.D(ramData), .en(decoder_1_out3), .clk(Clk), .Q(reg2_q), .clr(rst));
  assign controlled_buffer_1_out = decoder_1_out4 ? reg1_q : 8'bz;  // Controlled_Buffer controlled_buffer_1
  assign controlled_buffer_1_out = decoder_1_out5 ? reg2_q : 8'bz;  // Controlled_Buffer controlled_buffer_2
  Subtractor subtractor_1 (.a(reg1_q), .b(reg2_q), .out(subtractor_1_out));  // open: bin, bout
  Multiplier multiplier_1 (.a(reg1_q), .b(reg2_q), .out(multiplier_1_out));  // open: cin, cout
  Divider divider_1 (.a(reg1_q), .b(reg2_q), .out(divider_1_out), .rem(divider_1_rem));  // open: upper
  Adder adder_1 (.a(reg1_q), .b(reg2_q), .out(adder_1_out));  // open: cin, cout
  assign controlled_buffer_1_out = decoder_1_out6 ? adder_1_out : 8'bz;  // Controlled_Buffer controlled_buffer_3
  assign controlled_buffer_1_out = decoder_1_out7 ? multiplier_1_out : 8'bz;  // Controlled_Buffer controlled_buffer_4
  assign controlled_buffer_1_out = decoder_1_out8 ? divider_1_out : 8'bz;  // Controlled_Buffer controlled_buffer_5
  assign controlled_buffer_1_out = decoder_1_out11 ? divider_1_rem : 8'bz;  // Controlled_Buffer controlled_buffer_6
  assign controlled_buffer_1_out = decoder_1_out12 ? subtractor_1_out : 8'bz;  // Controlled_Buffer controlled_buffer_7
  Comparator comparator_1 (.a(reg1_q), .b(reg2_q), .eq(comparator_1_eq));  // open: gt, lt
  or or_2 (or_2_out, jie, jine);
  and and_1 (jie, comparator_1_eq, decoder_1_out9);
  not not_1 (not_1_out, comparator_1_eq);
  and and_2 (jine, not_1_out, decoder_1_out10);
  Counter counter_1 (
    .clr(rst), .load(or_2_out), .count(oo), .clk(Clk), .D(rom_1_data), .Q(counter_1_q));  // open: up, carry
  Decoder #(.select(4)) decoder_1 (
    .out2(decoder_1_out2), .out3(decoder_1_out3), .out4(decoder_1_out4), .out5(decoder_1_out5),
    .out6(decoder_1_out6), .out7(decoder_1_out7), .out8(decoder_1_out8), .out9(decoder_1_out9),
    .out10(decoder_1_out10), .out11(decoder_1_out11), .out12(decoder_1_out12), .out13(LVRAM1), .out14(print),
    .sel(rom_1_data_2));  // open: out0, out1, out15, en
  ROM #(.dataWidth(12)) rom_1 (.addr(counter_1_q), .data({rom_1_data_2, rom_1_data}));
  Counter counter_2 (.count(LVRAM1), .clk(Clk), .Q(counter_2_q));  // open: clr, load, up, D, carry
  Adder adder_2 (.a(ramData), .b(8'h25), .out(adder_2_out));  // open: cin, cout
  RAM #(.clearpin("true"), .enables("line")) ram_2 (
    .addr(counter_2_q), .we(LVRAM1), .clk(Clk), .din(adder_2_out), .dout(ram_2_dout));  // open: clr
  TTY tty_1 (.data(ram_2_dout[6:0]), .clk(Clk), .we(or_3_out));  // open: clr
  not not_2 (nullChar, or_3_out);
  or or_3 (or_3_out, ram_2_dout[0], ram_2_dout[1], ram_2_dout[2], ram_2_dout[3], ram_2_dout[4], ram_2_dout[5], ram_2_dout[6]);

  // Notes on the sheet:
  //   contents of rom_1 (hex, n*v repeats v):
  //   200 301 500 601 202 303 c02 202 a00 201 301 90b
endmodule

module nie_udana_proba_1 (
  input  in_1,
  input  in_2
);

  wire and_1_out, and_2_out, Clk, decoder_1_out1, decoder_1_out2, decoder_1_out3, decoder_1_out4,
       decoder_1_out5, or_1_out, or_2_out;
  wire [3:0] adder_1_out, controlled_buffer_1_out, ram_1_dout, reg1_q, reg2_q, rom_1_data;
  wire [7:0] counter_1_q;
  wire [7:4] rom_1_data_2;

  RAM #(.addrWidth(4), .dataWidth(4), .readbehav("war")) ram_1 (
    .addr(rom_1_data_2), .we(or_1_out), .oe(or_2_out), .clk(Clk), .din(controlled_buffer_1_out),
    .dout(ram_1_dout));
  Clock u_clk (.out(Clk));
  Register #(.width(4)) reg1 (.D(ram_1_dout), .clk(and_1_out), .Q(reg1_q), .clr(in_2));  // open: en
  and and_1 (and_1_out, decoder_1_out1, Clk);
  or or_1 (or_1_out, decoder_1_out4, decoder_1_out5, decoder_1_out3);
  or or_2 (or_2_out, decoder_1_out1, decoder_1_out2);
  assign controlled_buffer_1_out = decoder_1_out3 ? reg1_q : 4'bz;  // Controlled_Buffer controlled_buffer_1
  Register #(.width(4)) reg2 (.D(ram_1_dout), .clk(and_2_out), .Q(reg2_q), .clr(in_2));  // open: en
  and and_2 (and_2_out, decoder_1_out2, Clk);
  Adder #(.width(4)) adder_1 (.a(reg1_q), .b(reg2_q), .out(adder_1_out));  // open: cin, cout
  assign controlled_buffer_1_out = decoder_1_out5 ? adder_1_out : 4'bz;  // Controlled_Buffer controlled_buffer_2
  assign controlled_buffer_1_out = decoder_1_out4 ? reg2_q : 4'bz;  // Controlled_Buffer controlled_buffer_3
  Multiplier multiplier_1 ();  // open: a, b, out, cin, cout
  Counter counter_1 (.clr(in_2), .count(in_1), .clk(Clk), .Q(counter_1_q));  // open: load, up, D, carry
  Decoder #(.select(4)) decoder_1 (
    .out1(decoder_1_out1), .out2(decoder_1_out2), .out3(decoder_1_out3), .out4(decoder_1_out4),
    .out5(decoder_1_out5), .sel(rom_1_data));  // open: out0, out6, out7, out8, out9, out10, out11, out12, out13, out14, out15, en
  ROM rom_1 (.addr(counter_1_q), .data({rom_1_data_2, rom_1_data}));

  // Other names for the same wires on the sheet: rst = in_2

  // Notes on the sheet:
  //   contents of rom_1 (hex, n*v repeats v):
  //   0 11 22 35 11 22 45
endmodule

module main (
  output out_1
);

  wire and_1_out, and_4_out, bitfinder_1_found, button_2_out, clock_1_out, clock_2_out, clock_3_out,
       clock_4_out, clock_5_out, clock_6_out, clock_7_out, clock_8_out, clock_9_out, clock_10_out, clr_print,
       controller_1_print, controller_1_put_char, d_ff_1_qn, d_ff_2_q, jump, not_1_out, not_printing,
       or_1_out, or_2_out, or_3_out, or_4_out, print, printing, put_char, pwr, rst, wrt_r1, wrt_r2, wrt_ram;
  wire [3:0] instruction;
  wire [7:0] addr, address, counter_1_q, curr_vRam_addr, out_ram, r1, r2, ram_1_dout, wrt_data;

  Button button_1 (.out(rst));
  Button button_2 (.out(button_2_out));
  D_Flip_Flop d_ff_1 (.D(d_ff_1_qn), .clk(button_2_out), .Q(pwr), .Qn(d_ff_1_qn));  // open: preset, reset
  Counter counter_1 (
    .clr(rst), .load(jump), .count(pwr), .clk(clock_1_out), .D(address), .Q(counter_1_q));  // open: up, carry
  Clock clock_1 (.out(clock_1_out));
  D_Flip_Flop d_ff_2 (.D(printing), .clk(clock_2_out), .Q(d_ff_2_q));  // open: Qn, preset, reset
  Clock clock_2 (.out(clock_2_out));
  or or_1 (or_1_out, clr_print, rst);
  Counter counter_2 (
    .clr(or_1_out), .up(not_printing), .count(or_2_out), .clk(clock_3_out), .Q(curr_vRam_addr));  // open: load, D, carry
  or or_2 (or_2_out, put_char, printing);
  Clock clock_3 (.out(clock_3_out));
  J_K_Flip_Flop j_k_ff_1 (.J(and_1_out), .K(clr_print), .clk(clock_4_out), .Q(clr_print));  // open: Qn, preset, reset
  and and_1 (and_1_out, not_printing, d_ff_2_q);
  Clock clock_4 (.out(clock_4_out));
  ROM #(.dataWidth(12)) rom_1 (.addr(counter_1_q), .data({instruction, address}));
  Clock clock_5 (.out(clock_5_out));
  controller controller_1 (
    .pwr(pwr), .instruction(instruction), .reg_1(r1), .reg_2(r2), .address(address), .printing(printing),
    .wrt_out(wrt_data), .wrt(wrt_ram), .addr(addr), .to_reg_1(wrt_r1), .to_reg_2(wrt_r2), .jump(jump),
    .print(controller_1_print), .put_char(controller_1_put_char), .was_err(out_1));
  or or_3 (or_3_out, rst, clr_print);
  RAM #(.clearpin("true"), .enables("line")) ram_1 (
    .addr(curr_vRam_addr), .we(put_char), .clk(clock_5_out), .din(out_ram), .dout(ram_1_dout), .clr(or_3_out));
  and and_2 (print, controller_1_print, not_printing);
  and and_3 (put_char, controller_1_put_char, not_printing);
  Clock clock_6 (.out(clock_6_out));
  BitFinder #(.\type ("low0")) bitfinder_1 (.in(curr_vRam_addr), .found(bitfinder_1_found));  // open: index
  not not_1 (not_1_out, bitfinder_1_found);
  TTY tty_1 (.data(ram_1_dout[6:0]), .clk(clock_6_out), .we(printing), .clr(rst));
  T_Flip_Flop t_ff_1 (.T(or_4_out), .clk(clock_7_out), .Q(printing), .Qn(not_printing));  // open: reset, preset
  or or_4 (or_4_out, print, and_4_out);
  and and_4 (and_4_out, not_1_out, printing);
  Clock clock_7 (.out(clock_7_out));
  Register reg1 (.D(out_ram), .en(wrt_r1), .clk(clock_8_out), .Q(r1), .clr(rst));
  Clock clock_8 (.out(clock_8_out));
  Clock clock_9 (.out(clock_9_out));
  RAM #(.enables("line")) ram_2 (.addr(addr), .we(wrt_ram), .clk(clock_9_out), .din(wrt_data), .dout(out_ram));
  Register reg2 (.D(out_ram), .en(wrt_r2), .clk(clock_10_out), .Q(r2), .clr(rst));
  Clock clock_10 (.out(clock_10_out));

  // Notes on the sheet:
  //   contents of rom_1 (hex, n*v repeats v):
  //   0 101 408 f08 8 108 906 0 d04 d05 d06 e00 8 108 90e
endmodule

module controller (
  input  pwr,
  input  [3:0] instruction,
  input  [7:0] reg_1,
  input  [7:0] reg_2,
  input  [7:0] address,
  input  printing,
  output [7:0] wrt_out,
  output wrt,
  output [7:0] addr,
  output to_reg_1,
  output to_reg_2,
  output jump,
  output print,
  output put_char,
  output was_err
);

  wire alu_1_err, and_1_out, and_2_out, and_3_out, and_4_out, clock_1_out, eq_1_equal, jump_on_err,
       not_1_out, or_2_out, or_3_out, take_xor, w_r2_w_r1;
  wire [1:0] jumps;
  wire [2:0] memory;
  wire [4:0] equasions;
  wire [7:0] eq_1_xor_out;

  or or_1 (to_reg_2, memory[2], w_r2_w_r1);
  assign wrt_out = memory[1] ? reg_1 : 8'bz;  // Controlled_Buffer controlled_buffer_1
  or or_2 (or_2_out, print, put_char);
  assign wrt_out = memory[0] ? reg_2 : 8'bz;  // Controlled_Buffer controlled_buffer_2
  alu alu_1 (.r1(reg_1), .r2(reg_2), .dzialanie(equasions), .wynik(wrt_out), .err(alu_1_err));
  Decoder #(.select(4)) decoder_1 (
    .out0(to_reg_1), .out1(memory[2]), .out2(memory[1]), .out3(memory[0]), .out4(equasions[4]),
    .out5(equasions[3]), .out6(equasions[2]), .out7(equasions[1]), .out8(equasions[0]), .out9(jumps[1]),
    .out10(jumps[0]), .out11(take_xor), .out12(w_r2_w_r1), .out13(put_char), .out14(print),
    .out15(jump_on_err), .sel(instruction), .en(pwr));
  or or_3 (or_3_out, alu_1_err, and_1_out);
  Clock clock_1 (.out(clock_1_out));
  and and_1 (and_1_out, printing, or_2_out);
  D_Flip_Flop d_ff_1 (.D(or_3_out), .clk(clock_1_out), .Q(was_err));  // open: Qn, preset, reset
  or or_4 (wrt, memory[1], memory[0], equasions[0], equasions[1], equasions[2], equasions[3], equasions[4]);
  and and_2 (and_2_out, jump_on_err, was_err);
  not not_1 (not_1_out, w_r2_w_r1);
  eq eq_1 (.input_1(reg_1), .input_2(reg_2), .equal(eq_1_equal), .xOR_out(eq_1_xor_out));
  assign wrt_out = take_xor ? eq_1_xor_out : 8'bz;  // Controlled_Buffer controlled_buffer_3
  assign addr = w_r2_w_r1 ? reg_1 : 8'bz;  // Controlled_Buffer controlled_buffer_4
  assign addr = not_1_out ? address : 8'bz;  // Controlled_Buffer controlled_buffer_5
  and and_3 (and_3_out, jumps[1], eq_1_equal);
  or or_5 (jump, and_3_out, and_2_out, and_4_out);
  and and_4 (and_4_out, ~eq_1_equal, jumps[0]);  // AND_Gate

  // Other names for the same wires on the sheet: memory[3] = to_reg_1; print_action[1:0] = {put_char, print};
  //   reg1[7:0] = reg_1; reg2[7:0] = reg_2; alu_out[7:0] = wrt_out; reg_out[7:0] = wrt_out; xor_o[7:0] = wrt_out

  // Notes on the sheet:
  //   Write to memory reg1/2
endmodule

module alu (
  input  [7:0] r1,
  input  [7:0] r2,
  input  [4:0] dzialanie,
  output [7:0] wynik,
  output err
);

  wire adder_1_cout, and_1_out, and_2_out, and_3_out, bitfinder_1_found, bitfinder_2_found, not_1_out;
  wire [7:0] adder_1_out, divider_1_out, divider_1_rem, multiplier_1_cout, multiplier_1_out, subtractor_1_out;

  Adder adder_1 (.a(r1), .b(r2), .out(adder_1_out), .cout(adder_1_cout));  // open: cin
  Subtractor subtractor_1 (.a(r1), .b(r2), .out(subtractor_1_out));  // open: bin, bout
  Multiplier multiplier_1 (.a(r1), .b(r2), .out(multiplier_1_out), .cout(multiplier_1_cout));  // open: cin
  assign wynik = dzialanie[1] ? divider_1_out : 8'bz;  // Controlled_Buffer controlled_buffer_1
  Divider divider_1 (.a(r1), .b(r2), .out(divider_1_out), .rem(divider_1_rem));  // open: upper
  assign wynik = dzialanie[0] ? divider_1_rem : 8'bz;  // Controlled_Buffer controlled_buffer_2
  assign wynik = dzialanie[4] ? adder_1_out : 8'bz;  // Controlled_Buffer controlled_buffer_3
  assign wynik = dzialanie[3] ? subtractor_1_out : 8'bz;  // Controlled_Buffer controlled_buffer_4
  assign wynik = dzialanie[2] ? multiplier_1_out : 8'bz;  // Controlled_Buffer controlled_buffer_5
  BitFinder bitfinder_1 (.in(divider_1_rem), .found(bitfinder_1_found));  // open: index
  not not_1 (not_1_out, bitfinder_1_found);
  BitFinder bitfinder_2 (.in(multiplier_1_cout), .found(bitfinder_2_found));  // open: index
  and and_1 (and_1_out, adder_1_cout, dzialanie[4]);
  and and_2 (and_2_out, dzialanie[2], bitfinder_2_found);
  and and_3 (and_3_out, dzialanie[0], not_1_out);
  or or_1 (err, and_1_out, and_3_out, and_2_out);
endmodule

module eq (
  input  [7:0] input_1,
  input  [7:0] input_2,
  output equal,
  output [7:0] xOR_out
);

  wire or_1_out;

  xor xor_1 (xOR_out[0], input_1[0], input_2[0]);
  xor xor_2 (xOR_out[1], input_1[1], input_2[1]);
  xor xor_3 (xOR_out[2], input_1[2], input_2[2]);
  xor xor_4 (xOR_out[3], input_1[3], input_2[3]);
  xor xor_5 (xOR_out[4], input_1[4], input_2[4]);
  xor xor_6 (xOR_out[5], input_1[5], input_2[5]);
  xor xor_7 (xOR_out[6], input_1[6], input_2[6]);
  xor xor_8 (xOR_out[7], input_1[7], input_2[7]);
  or or_1 (or_1_out, xOR_out[0], xOR_out[1], xOR_out[2], xOR_out[3], xOR_out[4], xOR_out[5], xOR_out[6], xOR_out[7]);
  not not_1 (equal, or_1_out);
endmodule
